# Fritzing sketch SafetyBox (saved by Fritzing 0.8.7b)
breadboards: 1

parts:
  U3 = NodeMCU V1.0
  Part1 = SRF05 Ultrasonic Rangefinder
  Part2 = RFID-RC522-v2
  Display1 = LCD screen 16x2 IIC [part_number=101290]

nets:
  N1: U3.D0, Part1.Trig
  N2: U3.D1, Display1.SCL
  N3: U3.D2, Display1.SDA
  N4: U3.D3, Part2.RST
  N5: U3.D4, Part2.SDA
  3V3: U3.3V3, Part1.VCC, Part2.3.3V
  GND: U3.GND, Part1.GND, Part2.GND
  N6: U3.D5, Part2.SCK
  N7: U3.D6, Part2.MISO
  N8: U3.D7, Part2.MOSI
  N9: U3.D8, Part1.Echo

custom parts:
  NodeMCU V1.0: ESP8266 based NodeMCU
  RFID-RC522-v2: A simple China made RFID-RC522 Reader; do check the pin labels, as this is a MFRC522 based clone.
  LCD screen 16x2 IIC: LCD screen with HD44780 controller enables showing text, symbols, value or anything else that comes from Croduino/Arduino. It is capable of showing 16 symbols in two lines and therefore can be used in many projects that need to send clearly visible and legible output information.. • Color of symbols: White • Backlight: Blue • Dimensions: 80 x 36 x 12 mm • Screen dimensions: 64.5 x 16 mm •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
